// Logisim project 3to8.circ as structural Verilog: 2 circuits, main circuit main
module main (
  input  in_1,
  input  in_2,
  input  in_3,
  output out_4,
  output out_5,
  output out_6,
  output out_7,
  output out_8,
  output out_9,
  output out_10,
  output out_11
);

  subcircuit subcircuit_1 (
    .A0(in_1), .A1(in_2), .A3(in_3), .D0(out_4), .D1(out_5), .D2(out_6), .D3(out_7), .D4(out_8), .D5(out_10),
    .D6(out_11), .D7(out_9));
endmodule

module subcircuit (
  input  A0,
  input  A1,
  input  A3,
  output D0,
  output D1,
  output D2,
  output D3,
  output D4,
  output D5,
  output D6,
  output D7
);

  wire not_1_out, not_2_out, not_3_out;

  not not_1 (not_1_out, A0);
  not not_2 (not_2_out, A1);
  not not_3 (not_3_out, A3);
  and and_1 (D0, A0, A1, A3);
  and and_2 (D1, A0, A1, not_3_out);
  and and_3 (D2, A0, not_2_out, A3);
  and and_4 (D3, A0, not_2_out, not_3_out);
  and and_5 (D4, not_1_out, A1, A3);
  and and_6 (D5, not_1_out, A1, not_3_out);
  and and_7 (D6, not_1_out, not_2_out, A3);
  and and_8 (D7, not_1_out, not_2_out, not_3_out);
endmodule
