// Logisim project 4to16_subcircuit.circ as structural Verilog: 2 circuits, main circuit main
module main (
  input  A0,
  input  A1,
  input  A2,
  input  A3,
  output D0,
  output D1,
  output D2,
  output D3,
  output D4,
  output D5,
  output D6,
  output D7,
  output D8,
  output D15,
  output D9,
  output D10,
  output D11,
  output D13,
  output D14,
  output D12
);

  subcircuit subcircuit_1 (
    .D0(D0), .D1(D1), .D2(D2), .D3(D3), .D4(D4), .D5(D5), .D6(D6), .D7(D7), .D8(D8), .D9(D9), .D10(D10),
    .D11(D11), .D12(D12), .D13(D13), .D14(D14), .D15(D15), .A0(A0), .A1(A1), .A2(A2), .A3(A3));
endmodule

module subcircuit (
  input  A0,
  input  A1,
  input  A2,
  input  A3,
  output D0,
  output D1,
  output D2,
  output D3,
  output D4,
  output D5,
  output D6,
  output D7,
  output D8,
  output D9,
  output D10,
  output D11,
  output D12,
  output D13,
  output D14,
  output D15
);

  wire not_1_out, not_2_out, not_3_out, not_4_out;

  not not_1 (not_1_out, A0);
  not not_2 (not_2_out, A1);
  not not_3 (not_3_out, A2);
  not not_4 (not_4_out, A3);
  and and_1 (D0, A0, A1, A2, A3);
  and and_2 (D1, A0, A1, A2, not_4_out);
  and and_3 (D2, A0, A1, not_3_out, A3);
  and and_4 (D3, A0, A1, not_3_out, not_4_out);
  and and_5 (D4, A0, not_2_out, A2, A3);
  and and_6 (D5, A0, not_2_out, A2, not_4_out);
  and and_7 (D6, A0, not_2_out, not_3_out, A3);
  and and_8 (D7, A0, not_2_out, not_3_out, not_4_out);
  and and_9 (D8, not_1_out, A1, A2, A3);
  and and_10 (D9, not_1_out, A1, A2, not_4_out);
  and and_11 (D10, not_1_out, A1, not_3_out, A3);
  and and_12 (D11, not_1_out, A1, not_3_out, not_4_out);
  and and_13 (D12, not_1_out, not_2_out, A2, A3);
  and and_14 (D13, not_1_out, not_2_out, A2, not_4_out);
  and and_15 (D14, not_1_out, not_2_out, not_3_out, A3);
  and and_16 (D15, not_1_out, not_2_out, not_3_out, not_4_out);
endmodule
