// Logisim project W4_LAB.circ as structural Verilog: 1 circuit, main circuit main
module main (
  input  D,
  output Q
);

  wire clock_1_out, nand_1_out, nand_2_out, nand_4_out;

  Clock clock_1 (.out(clock_1_out));
  nand nand_1 (nand_1_out, D, clock_1_out);
  nand nand_2 (nand_2_out, nand_1_out, clock_1_out);
  nand nand_3 (Q, nand_1_out, nand_4_out);
  nand nand_4 (nand_4_out, Q, nand_2_out);

  // Notes on the sheet:
  //   CLK
  //   D Latch (NAND)
endmodule
