// Logisim project W4_Task 3.circ as structural Verilog: 1 circuit, main circuit main
module main (
  input  in_1,
  input  in_2,
  input  in_3,
  input  in_4,
  input  in_5,
  input  in_6,
  input  in_7,
  input  in_8,
  input  S1,
  input  S2,
  input  S3,
  input  Clock,
  output out_13,
  output out_14,
  output out_15,
  output out_16,
  output out_17,
  output out_18,
  output out_19,
  output out_20
);

  wire and_1_out, and_2_out, and_3_out, and_4_out, and_5_out, and_6_out, and_7_out, and_8_out,
       subcircuit_1_d0, subcircuit_1_d1, subcircuit_1_d2, subcircuit_1_d3, subcircuit_1_d4, subcircuit_1_d5,
       subcircuit_1_d6, subcircuit_1_d7;
  wire [2:0] not_3_out;
  wire [7:0] main_1_q0, main_2_q0, main_3_q0, main_4_q0, main_5_q0, main_6_q0, main_7_q0, main_8_q0;

  not not_1 (not_3_out[2], S1);
  not not_2 (not_3_out[1], S2);
  not not_3 (not_3_out[0], S3);
  subcircuit subcircuit_1 (
    .A0(S1), .A1(S2), .A3(S3), .D0(subcircuit_1_d0), .D1(subcircuit_1_d1), .D2(subcircuit_1_d2),
    .D3(subcircuit_1_d3), .D4(subcircuit_1_d4), .D5(subcircuit_1_d5), .D6(subcircuit_1_d6),
    .D7(subcircuit_1_d7));
  and and_1 (and_1_out, Clock, subcircuit_1_d0);
  and and_2 (and_2_out, Clock, subcircuit_1_d1);
  and and_3 (and_3_out, Clock, subcircuit_1_d2);
  and and_4 (and_4_out, Clock, subcircuit_1_d3);
  and and_5 (and_5_out, Clock, subcircuit_1_d4);
  and and_6 (and_6_out, Clock, subcircuit_1_d7);
  and and_7 (and_7_out, Clock, subcircuit_1_d5);
  and and_8 (and_8_out, Clock, subcircuit_1_d6);
  W4_Task_2_main main_1 (
    .D0(in_1), .D1(in_2), .D2(in_3), .D3(in_4), .D4(in_5), .D5(in_6), .D6(in_7), .D7(in_8), .in_9(and_1_out),
    .Q0(main_1_q0[0]), .Q1(main_1_q0[1]), .Q5(main_1_q0[2]), .Q1_2(main_1_q0[3]), .Q6(main_1_q0[4]),
    .Q1_3(main_1_q0[5]), .Q4(main_1_q0[6]), .Q7(main_1_q0[7]));
  W4_Task_2_main main_2 (
    .D0(in_1), .D1(in_2), .D2(in_3), .D3(in_4), .D4(in_5), .D5(in_6), .D6(in_7), .D7(in_8), .in_9(and_2_out),
    .Q0(main_2_q0[0]), .Q1(main_2_q0[1]), .Q5(main_2_q0[2]), .Q1_2(main_2_q0[3]), .Q6(main_2_q0[4]),
    .Q1_3(main_2_q0[5]), .Q4(main_2_q0[6]), .Q7(main_2_q0[7]));
  W4_Task_2_main main_3 (
    .D0(in_1), .D1(in_2), .D2(in_3), .D3(in_4), .D4(in_5), .D5(in_6), .D6(in_7), .D7(in_8), .in_9(and_3_out),
    .Q0(main_3_q0[0]), .Q1(main_3_q0[1]), .Q5(main_3_q0[2]), .Q1_2(main_3_q0[3]), .Q6(main_3_q0[4]),
    .Q1_3(main_3_q0[5]), .Q4(main_3_q0[6]), .Q7(main_3_q0[7]));
  W4_Task_2_main main_4 (
    .D0(in_1), .D1(in_2), .D2(in_3), .D3(in_4), .D4(in_5), .D5(in_6), .D6(in_7), .D7(in_8), .in_9(and_4_out),
    .Q0(main_4_q0[0]), .Q1(main_4_q0[1]), .Q5(main_4_q0[2]), .Q1_2(main_4_q0[3]), .Q6(main_4_q0[4]),
    .Q1_3(main_4_q0[5]), .Q4(main_4_q0[6]), .Q7(main_4_q0[7]));
  W4_Task_2_main main_5 (
    .D0(in_1), .D1(in_2), .D2(in_3), .D3(in_4), .D4(in_5), .D5(in_6), .D6(in_7), .D7(in_8), .in_9(and_5_out),
    .Q0(main_5_q0[0]), .Q1(main_5_q0[1]), .Q5(main_5_q0[2]), .Q1_2(main_5_q0[3]), .Q6(main_5_q0[4]),
    .Q1_3(main_5_q0[5]), .Q4(main_5_q0[6]), .Q7(main_5_q0[7]));
  W4_Task_2_main main_6 (
    .D0(in_1), .D1(in_2), .D2(in_3), .D3(in_4), .D4(in_5), .D5(in_6), .D6(in_7), .D7(in_8), .in_9(and_6_out),
    .Q0(main_6_q0[0]), .Q1(main_6_q0[1]), .Q5(main_6_q0[2]), .Q1_2(main_6_q0[3]), .Q6(main_6_q0[4]),
    .Q1_3(main_6_q0[5]), .Q4(main_6_q0[6]), .Q7(main_6_q0[7]));
  W4_Task_2_main main_7 (
    .D0(in_1), .D1(in_2), .D2(in_3), .D3(in_4), .D4(in_5), .D5(in_6), .D6(in_7), .D7(in_8), .in_9(and_7_out),
    .Q0(main_7_q0[0]), .Q1(main_7_q0[1]), .Q5(main_7_q0[2]), .Q1_2(main_7_q0[3]), .Q6(main_7_q0[4]),
    .Q1_3(main_7_q0[5]), .Q4(main_7_q0[6]), .Q7(main_7_q0[7]));
  W4_Task_2_main main_8 (
    .D0(in_1), .D1(in_2), .D2(in_3), .D3(in_4), .D4(in_5), .D5(in_6), .D6(in_7), .D7(in_8), .in_9(and_8_out),
    .Q0(main_8_q0[0]), .Q1(main_8_q0[1]), .Q5(main_8_q0[2]), .Q1_2(main_8_q0[3]), .Q6(main_8_q0[4]),
    .Q1_3(main_8_q0[5]), .Q4(main_8_q0[6]), .Q7(main_8_q0[7]));
  Multiplexer #(.select(3), .width(8), .enable("false")) multiplexer_1 (
    .in0(main_1_q0), .in1(main_2_q0), .in2(main_3_q0), .in3(main_4_q0), .in4(main_5_q0), .in5(main_6_q0),
    .in6(main_7_q0), .in7(main_8_q0), .out({out_20, out_19, out_18, out_17, out_16, out_15, out_14, out_13}),
    .sel(not_3_out));
endmodule
