// Logisim project W4_Task 2.circ as structural Verilog: 2 circuits, main circuit main
module main (
  input  D0,
  input  D1,
  input  D2,
  input  D3,
  input  D4,
  input  D5,
  input  D6,
  input  D7,
  input  in_9,
  output Q0,
  output Q1,
  output Q5,
  output Q1_2,
  output Q6,
  output Q1_3,
  output Q4,
  output Q7
);

  subcircuit subcircuit_1 (
    .D0(D0), .D1(D1), .D2(D2), .D3(D3), .D4(D4), .D5(D5), .D6(D6), .D7(D7), .Q0(Q0), .Q1(Q1), .Q2(Q5),
    .Q3(Q1_2), .Q4(Q6), .Q5(Q1_3), .Q6(Q4), .Q7(Q7), .in_9(in_9));
endmodule

module subcircuit (
  input  D0,
  input  D1,
  input  D2,
  input  D3,
  input  D4,
  input  D5,
  input  D6,
  input  D7,
  input  in_9,
  output Q0,
  output Q1,
  output Q2,
  output Q3,
  output Q4,
  output Q5,
  output Q6,
  output Q7
);

  wire nand_1_out, nand_2_out, nand_3_out, nand_4_out, nand_5_out, nand_6_out, nand_7_out, nand_8_out,
       nand_9_out, nand_10_out, nand_11_out, nand_12_out, nand_13_out, nand_14_out, nand_15_out, nand_16_out,
       nand_18_out, nand_20_out, nand_22_out, nand_24_out, nand_26_out, nand_28_out, nand_30_out, nand_32_out;

  nand nand_1 (nand_1_out, D0, in_9);
  nand nand_2 (nand_2_out, nand_1_out, in_9);
  nand nand_3 (nand_3_out, D1, in_9);
  nand nand_4 (nand_4_out, nand_3_out, in_9);
  nand nand_5 (nand_5_out, D2, in_9);
  nand nand_6 (nand_6_out, nand_5_out, in_9);
  nand nand_7 (nand_7_out, D3, in_9);
  nand nand_8 (nand_8_out, nand_7_out, in_9);
  nand nand_9 (nand_9_out, D4, in_9);
  nand nand_10 (nand_10_out, nand_9_out, in_9);
  nand nand_11 (nand_11_out, D5, in_9);
  nand nand_12 (nand_12_out, nand_11_out, in_9);
  nand nand_13 (nand_13_out, D6, in_9);
  nand nand_14 (nand_14_out, nand_13_out, in_9);
  nand nand_15 (nand_15_out, D7, in_9);
  nand nand_16 (nand_16_out, nand_15_out, in_9);
  nand nand_17 (Q0, nand_1_out, nand_18_out);
  nand nand_18 (nand_18_out, Q0, nand_2_out);
  nand nand_19 (Q1, nand_3_out, nand_20_out);
  nand nand_20 (nand_20_out, Q1, nand_4_out);
  nand nand_21 (Q2, nand_5_out, nand_22_out);
  nand nand_22 (nand_22_out, Q2, nand_6_out);
  nand nand_23 (Q3, nand_7_out, nand_24_out);
  nand nand_24 (nand_24_out, Q3, nand_8_out);
  nand nand_25 (Q4, nand_9_out, nand_26_out);
  nand nand_26 (nand_26_out, Q4, nand_10_out);
  nand nand_27 (Q5, nand_11_out, nand_28_out);
  nand nand_28 (nand_28_out, Q5, nand_12_out);
  nand nand_29 (Q6, nand_13_out, nand_30_out);
  nand nand_30 (nand_30_out, Q6, nand_14_out);
  nand nand_31 (Q7, nand_15_out, nand_32_out);
  nand nand_32 (nand_32_out, Q7, nand_16_out);
endmodule
